# Fritzing sketch Basic Sketch (saved by Fritzing 0.9.3b)
perfboards: 1
breadboards: 1

parts:
  Part1 = Arduino Nano (Rev3.0) (ICSP)
  hc-sr1 = hc-sr04
  JP1 = Header 2 [package=molex-1x2_lock]
  JP2 = Header 2 [package=molex-1x2_lock]
  J1 = male pin header, 4 pins [form="♂ (male)"]
  U1 = 555 Timer [package="DIP8 [THT]"]  # not connected
  M1 = DC Motor
  M2 = DC Motor
  VCC1 = 4 x AAA Battery Mount  # not connected

nets:
  GND: Part1.GND, hc-sr1.GND
  N1: Part1.D5, JP2.1
  N2: Part1.D6, JP2.2
  N3: Part1.D9, JP1.2
  N4: Part1.D10, JP1.1
  N5: Part1.D12/MISO, hc-sr1.Echo
  5V: Part1.5V, hc-sr1.VCC
  N6: Part1.D13/SCK, hc-sr1.Trig
  N7: J1.pin1, M2.pin_2
  N8: J1.pin2, M2.pin_1
  N9: J1.pin3, M1.pin_2
  N10: J1.pin4, M1.pin_1
